# Fritzing sketch desain-rancangan (saved by Fritzing 0.9.3b)
breadboards: 1

parts:
  A1 = ESP32 DevKitc V4
  Mod1 = KY-015 Temperature & Humidity Sensor Module [package="Breakout board"]
  M1 = mics-6814
  Part1 = BH1750

nets:
  N1: A1.Pin_1, Mod1.S, Part1.VCC
  N2: A1.Pin_5, M1.CO
  N3: A1.Pin_6, M1.NH3
  N4: A1.Pin_7, M1.NO2
  GND: A1.Pin_14, A1.Pin_32, A1.Pin_38, Mod1.-, M1.GND, Part1.GND
  N5: A1.Pin_19, M1.+5V
  N6: A1.Pin_26, Mod1.Vin
  N7: A1.Pin_33, Part1.SDA
  N8: A1.Pin_36, Part1.SCL

custom parts:
  ESP32 DevKitc V4: ESP32-DevKitC board with ESP32-WROOM-32 module. ESP32-DevKitC V4 is a small-sized ESP32-based development board produced by Espressif. Most of the pins on the ESP module are broken out to the pin headers on the board. The pins D0, D1, D2, D3, CMD and CLK are used internally for communication between ESP32 and SPI flash memory. They are grouped on both sides near the USB connector. Avoid using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
  KY-015 Temperature & Humidity Sensor Module: KY-015 temperature and humidity sensor module, provides a low-latency serial interface to measure humidity and temperature.
  mics-6814: The MICS6814 sensor comprises three semiconductor gas sensors in a single package, and can detect three different groups of gases that are referred to in the datasheet as reducing, oxidising, and NH3. The major gases/vapours that the sensor detects are: carbon monoxide (reducing), nitrogen dioxide (oxidising), and ammonia (NH3), but it is also sensitive to others, including hydrogen, ethanol,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
  BH1750: Light Sensor
